# Fritzing sketch test (saved by Fritzing 0.9.3b)
circuit board: 5.65133cm x 2.60535cm

parts:
  arduino = Arduino Pro Mini (5V)
  R1 = Resistor [package="2512 [SMD]"]
  R2 = Resistor [package="2512 [SMD]"]
  R3 = Resistor [package="2512 [SMD]"]
  R4 = Resistor [package="2512 [SMD]"]
  R5 = Resistor [tolerance=±5% resistance=220 package=THT]
  Q2 = MOSFET-NCHANNEL [package=to220v]
  S1 = Pushbutton [package=THT]
  S2 = Pushbutton [package=THT]
  S3 = Pushbutton [package=THT]
  Part1 = OLED Monochrome 128x32 I2C [part_number=931]

nets:
  N1: arduino.A4, Part1.SDA
  N2: arduino.A5, Part1.SCL
  GND: arduino.GND, R2.Pin_1, R3.Pin_1, S1.leg1, S2.leg1, S3.leg1, Part1.GND
  VCC: arduino.VCC, S1.leg0, S2.leg0, S3.leg0, Part1.VIN
  N3: arduino.MISO, R2.Pin_0
  N4: arduino.MOSI, R3.Pin_0
  N5: arduino.D7, R4.Pin_0
  N6: arduino.D4, Part1.RESET
  N7: arduino.D3, R5.Pin_0
  N8: R1.Pin_0, R5.Pin_1, Q2.G
  N9: R1.Pin_1, Q2.S

custom parts:
  Resistor: Resistor Basic schematic elements and footprints for 0603, 1206, and PTH resistors.
  OLED Monochrome 128x32 I2C: These displays are small, only about 1" diagonal, but very readable due to the high contrast of an OLED display. This display is made of 128x32 individual white OLED pixels, each one is turned on or off by the controller chip. Because the display makes its own light, no backlight is required. This reduces the power required to run the OLED and is why the display has such high contrast; we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
